# Fritzing sketch wiring_schematic (saved by Fritzing 0.7.1b)
breadboards: 1

parts:
  U1 = XBee
  Teensy1 = Teensy 2.0
  M1 = DC Motor
  M2 = DC Motor
  VCC1 = Battery block 9V
  VCC2 = Battery
  U2 = mystery part, 16 pins [chip_label=? spacing=300mil]

nets:
  VCC: U1.VCC, Teensy1.VCC, VCC2.+, U2.pin2
  N1: U1.pin2, Teensy1.D3
  N2: U1.pin3, Teensy1.D2
  GND: U1.pin5, U1.GND, Teensy1.GND, VCC2.-, U2.pin1, U2.pin9
  N3: Teensy1.C6, U2.pin10
  N4: Teensy1.C7, U2.pin16
  N5: Teensy1.D6, U2.pin15
  N6: Teensy1.D7, U2.pin14
  N7: Teensy1.B4, U2.pin13
  N8: Teensy1.B5, U2.pin12
  N9: Teensy1.B6, U2.pin11
  N10: M1.pin_1, U2.pin3
  N11: M1.pin_2, U2.pin4
  N12: M2.pin_1, U2.pin5
  N13: M2.pin_2, U2.pin6
  N14: VCC1.-, U2.pin8
  N15: VCC1.+, U2.pin7

notes:
  Note: this is actually this
  part: http://www.pololu.com/catalog/product/713
  but since Fritzing doesn't include this part, we can't
  really use it, hence the simple perfboard
